# Fritzing sketch CV_Amp (saved by Fritzing 0.9.4)
breadboards: 1

parts:
  IC1 = Dual Op-Amp [package=dip08]
  C1 = Ceramic Capacitor [capacitance=100nF package="100 mil [THT, multilayer]"]
  C2 = Ceramic Capacitor [capacitance=100nF package="100 mil [THT, multilayer]"]
  R1 = Rotary Potentiometer (Small) [maximum_resistance=100kΩ package=THT]
  R2 = Resistor [tolerance=±5% resistance=8.2k package=THT]
  R3 = Resistor [tolerance=±5% resistance=120k package=THT]
  R4 = Rotary Potentiometer (Small) [maximum_resistance=100kΩ package=THT]
  R5 = Resistor [tolerance=±5% resistance=10k package=THT]
  R6 = Resistor [tolerance=±5% resistance=22k package=THT]
  C3 = Electrolytic Capacitor [capacitance=1µF package="100 mil [THT, electrolytic]"]
  C4 = Electrolytic Capacitor [capacitance=1µF package="100 mil [THT, electrolytic]"]
  R7 = Resistor [tolerance=±5% resistance=1k package=THT]
  R8 = Resistor [tolerance=±5% resistance=1k package=THT]
  LED1 = LED - 3mm [color="Red (633nm)" package="3 mm [THT]"]
  LED2 = LED - 3mm [color="Blue (505nm)" package="3 mm [THT]"]

nets:
  N1: IC1.A_OUT, IC1.A_-IN, R2.Pin_1
  N2: IC1.A_+IN, R1.wiper
  N3: IC1.A_V-, C2.0, R4.leg1, C4.-, LED2.cathode
  N4: IC1.B_+IN, R2.Pin_0, R3.Pin_0
  N5: IC1.B_-IN, R5.Pin_1, R6.Pin_0
  N6: IC1.B_OUT, R6.Pin_1
  N7: IC1.A_V+, C1.0, R4.leg2, C3.+, LED1.anode
  N8: C1.1, C2.1, R1.leg1, R5.Pin_0, C3.-, C4.+, R7.Pin_0, R8.Pin_1
  N9: R3.Pin_1, R4.wiper
  N10: R7.Pin_1, LED1.cathode
  N11: R8.Pin_0, LED2.anode

notes:
  GND
  +12V
  -12V
  GND
  IN
  OUT
  BIAS
  50k/B
  LEVEL
  50k/A
